# Fritzing sketch demo_sketch (saved by Fritzing 0.8.3b)
circuit board: 8.72063cm x 5.54566cm
breadboards: 1

parts:
  BeagleBone1 = BeagleBone Black
  LED1 = LED - 5mm [color="Red (633nm)" package="5 mm [THT]"]
  LED2 = LED - 5mm [color="Yellow (595nm)" package="5 mm [THT]"]
  LED3 = LED - 5mm [color="Green (570nm)" package="5 mm [THT]"]
  R1 = Resistor [tolerance=±5% resistance=330 package=THT]
  R2 = Resistor [tolerance=±5% resistance=330 package=THT]
  R3 = Resistor [tolerance=±5% resistance=330 package=THT]
  S2 = Pushbutton [package="[THT]"]

nets:
  N1: BeagleBone1.no_name_yet#12, S2.Pin_1, S2.Pin_2
  N2: BeagleBone1.no_name_yet#14, R1.Pin_0
  N3: BeagleBone1.no_name_yet#16, R2.Pin_0
  N4: BeagleBone1.no_name_yet#22, R3.Pin_0
  GND: BeagleBone1.no_name_yet#45, LED1.cathode, LED2.cathode, LED3.cathode, S2.Pin_3, S2.Pin_4
  N5: LED1.anode, R1.Pin_1
  N6: LED2.anode, R2.Pin_1
  N7: LED3.anode, R3.Pin_1

custom parts:
  BeagleBone Black: BeagleBone Black rev. A5B
